# Fritzing sketch load balancer (saved by Fritzing 0.9.3b)

parts:
  Arduino_Nano = Arduino Nano (Rev3.0) (ICSP)
  Right_Servo = Basic Servo
  MPU_6050 = MPU-6050 Board GY-521 [form="♀ (female)" package=THT]
  HX711_ADC = Adafruit HX711 ADC Breakout [part_number=#5974]
  GML_692 = LOAD_CELL [package=1x03]
  GML_692_2 = LOAD_CELL [package=1x03]
  5v_GND = Header 12 [package=1x12_machine-pin-header_lock.004]
  5v = Header 12 [package=1x12_machine-pin-header_lock.004]
  9v = Header 12 [package=1x12_machine-pin-header_lock.004]
  9v_GND = Header 12 [package=1x12_machine-pin-header_lock.004]
  9v_Power = Battery block 9V
  Left_Servo = Basic Servo
  LED1 = LEDs [package=led10mm]
  LED2 = LEDs [package=led10mm]
  LED3 = LEDs [package=led10mm]
  LED4 = LEDs [package=led10mm]
  LED5 = LEDs [package=led10mm]
  LED6 = LEDs [package=led10mm]

nets:
  N1: Arduino_Nano.D2, LED1.A
  N2: Arduino_Nano.D3, LED2.A
  N3: Arduino_Nano.D4, LED3.A
  N4: Arduino_Nano.D5, LED4.A
  N5: Arduino_Nano.D6, LED6.A
  N6: Arduino_Nano.D7, LED5.A
  N7: Arduino_Nano.D9, Left_Servo.pulse
  N8: Arduino_Nano.D10, Right_Servo.pulse
  N9: Arduino_Nano.D11/MOSI, HX711_ADC.DATAOUT
  N10: Arduino_Nano.D12/MISO, HX711_ADC.SCLK
  N11: Arduino_Nano.GND, 5v_GND.1
  N12: Arduino_Nano.5V, 5v.1
  N13: Arduino_Nano.A5, MPU_6050.pin3
  N14: Arduino_Nano.A4, MPU_6050.pin4
  N15: Arduino_Nano.3V3, MPU_6050.pin1
  N16: Right_Servo.gnd, 9v_GND.10
  N17: Right_Servo.vcc, 9v.11
  N18: MPU_6050.pin2, 5v_GND.12
  N19: HX711_ADC.V+, 5v.12
  N20: HX711_ADC.GND, GML_692.R, GML_692_2.R, 5v_GND.11
  N21: HX711_ADC.VPP, GML_692.B, GML_692_2.B
  N22: HX711_ADC.B+, GML_692_2.W
  N23: HX711_ADC.A+, GML_692.W
  N24: 5v_GND.2, LED1.C
  N25: 5v_GND.3, LED2.C
  N26: 5v_GND.4, LED3.C
  N27: 5v_GND.5, LED4.C
  N28: 5v_GND.6, LED6.C
  N29: 5v_GND.7, LED5.C
  N30: 9v.1, 9v_Power.+
  N31: 9v.12, Left_Servo.vcc
  N32: 9v_GND.1, 9v_Power.-
  N33: 9v_GND.12, Left_Servo.gnd

custom parts:
  MPU-6050 Board GY-521: Acelerometro y Giroscopio MPU-6050 Board GY-521
  Adafruit HX711 ADC Breakout: If you are feeling the stress and strain of modern life a Wheatstone bridge and you want to quantify it, this handy breakout will do the job, no sweat! The Adafruit HX711 Breakout contains a super-high-resolution 24-Bit differential ADC with extra gain circuitry that makes it perfect for measuring strain gauges / load cells or other sensors that have four wires that are connected in a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
